# Fritzing sketch FritzingSheme (saved by Fritzing 0.9.5d)

parts:
  Mod1 = KY-022
  Компонент1 = Arduino Micro (Rev3)

nets:
  N1: Mod1.connector0, Компонент1.GND
  N2: Mod1.connector1, Компонент1.D2/SDA
  N3: Mod1.connector2, Компонент1.5V
